# Fritzing sketch Rocker-Bogie (saved by Fritzing 0.9.3b)
breadboards: 1

parts:
  Part1 = Arduino Uno (Rev3)
  U1 = LIPO-1000mAh [package=lipo-1000]
  M1 = DC Motor
  Q2 = Basic FET N-Channel [package="D2Pak [SMD]"]
  M2 = DC Motor
  M3 = DC Motor
  M4 = DC Motor
  M5 = DC Motor
  M6 = DC Motor
  Q3 = Basic FET N-Channel [package="D2Pak [SMD]"]
  J4 = Basic Servo
  J5 = Basic Servo
  J6 = Basic Servo
  J7 = Basic Servo

nets:
  N1: Part1.D9_PWM, J5.pulse
  N2: Part1.D10_PWM/SS, J4.pulse
  N3: Part1.D11_PWM/MOSI, J6.pulse
  N4: Part1.D3_PWM, Q2.Gate
  N5: Part1.D5_PWM, Q3.Gate
  N6: Part1.D6_PWM, J7.pulse
  VCC: U1.+, Q2.drain, Q3.drain, J4.vcc, J5.vcc, J6.vcc, J7.vcc
  GND: U1.-, M1.pin_2, M2.pin_2, M3.pin_2, M4.pin_2, M5.pin_2, M6.pin_2, J4.gnd, J5.gnd, J6.gnd, J7.gnd
  N7: M1.pin_1, Q2.source, M2.pin_1, M3.pin_1
  N8: M5.pin_1, M6.pin_1, Q3.source
